// Logisim project ALU32MIA27.circ as structural Verilog: 14 circuits, main circuit LeftShift32
module LeftShift32 (
  input  [31:0] B,
  input  [4:0] Sa,
  input  Cin,
  output [31:0] C
);

  wire [4:0] bit_extender_1_out;
  wire [31:0] eight_bit_shifter_1_cout, four_bit_shifter_1_cout, multiplexer_1_out, multiplexer_2_out,
       multiplexer_3_out, multiplexer_4_out, one_bit_shifter_1_cout, sixteen_bit_shifter_1_cout,
       two_bit_shifter_1_cout;

  assign bit_extender_1_out = {{4{Cin}}, Cin};  // Bit_Extender bit_extender_1
  Multiplexer #(.width(32), .enable("false")) multiplexer_1 (
    .in0(B), .in1(one_bit_shifter_1_cout), .out(multiplexer_1_out), .sel(Sa[0]));
  Multiplexer #(.width(32), .enable("false")) multiplexer_2 (
    .in0(multiplexer_1_out), .in1(two_bit_shifter_1_cout), .out(multiplexer_2_out), .sel(Sa[1]));
  Multiplexer #(.width(32), .enable("false")) multiplexer_3 (
    .in0(multiplexer_2_out), .in1(four_bit_shifter_1_cout), .out(multiplexer_3_out), .sel(Sa[2]));
  Multiplexer #(.width(32), .enable("false")) multiplexer_4 (
    .in0(multiplexer_3_out), .in1(eight_bit_shifter_1_cout), .out(multiplexer_4_out), .sel(Sa[3]));
  One_Bit_Shifter one_bit_shifter_1 (.Cin(bit_extender_1_out[0]), .B(B), .Cout(one_bit_shifter_1_cout));
  Two_Bit_Shifter two_bit_shifter_1 (.Cin(bit_extender_1_out[1]), .B(multiplexer_1_out), .Cout(two_bit_shifter_1_cout));
  Four_Bit_Shifter four_bit_shifter_1 (
    .Cin(bit_extender_1_out[2]), .B(multiplexer_2_out), .Cout(four_bit_shifter_1_cout));
  Eight_Bit_Shifter eight_bit_shifter_1 (
    .Cin(bit_extender_1_out[3]), .B(multiplexer_3_out), .Cout(eight_bit_shifter_1_cout));
  Sixteen_Bit_Shifter sixteen_bit_shifter_1 (
    .Cin(bit_extender_1_out[4]), .B(multiplexer_4_out), .Cout(sixteen_bit_shifter_1_cout));
  Multiplexer #(.width(32), .enable("false")) multiplexer_5 (
    .in0(multiplexer_4_out), .in1(sixteen_bit_shifter_1_cout), .out(C), .sel(Sa[4]));
endmodule

module One_Bit_Shifter (
  input  Cin,
  input  [31:0] B,
  output [31:0] Cout
);


  assign Cout = {B[30:0], Cin};
endmodule

module Two_Bit_Shifter (
  input  Cin,
  input  [31:0] B,
  output [31:0] Cout
);

  assign Cout[1:0] = {{1{Cin}}, Cin};  // Bit_Extender bit_extender_1

  assign Cout[31:2] = B[29:0];
endmodule

module Four_Bit_Shifter (
  input  Cin,
  input  [31:0] B,
  output [31:0] Cout
);

  assign Cout[3:0] = {{3{Cin}}, Cin};  // Bit_Extender bit_extender_1

  assign Cout[31:4] = B[27:0];
endmodule

module Eight_Bit_Shifter (
  input  Cin,
  input  [31:0] B,
  output [31:0] Cout
);

  assign Cout[7:0] = {{7{Cin}}, Cin};  // Bit_Extender bit_extender_1

  assign Cout[31:8] = B[23:0];
endmodule

module Sixteen_Bit_Shifter (
  input  Cin,
  input  [31:0] B,
  output [31:0] Cout
);

  assign Cout[15:0] = {{15{Cin}}, Cin};  // Bit_Extender bit_extender_1

  assign Cout[31:16] = B[15:0];
endmodule

module Add32 (
  input  [31:0] A,
  input  Cin,
  input  [31:0] B,
  output [31:0] C,
  output V
);

  wire four_bit_adder_1_cout, four_bit_adder_2_cout, four_bit_adder_3_cout, four_bit_adder_4_cout,
       four_bit_adder_5_cout, four_bit_adder_6_cout, four_bit_adder_7_cout;

  Four_Bit_Adder four_bit_adder_1 (.A(A[3:0]), .B(B[3:0]), .Cin(Cin), .S(C[3:0]), .Cout(four_bit_adder_1_cout));
  Four_Bit_Adder four_bit_adder_2 (
    .A(A[19:16]), .B(B[19:16]), .Cin(four_bit_adder_7_cout), .S(C[19:16]), .Cout(four_bit_adder_2_cout));
  Four_Bit_Adder four_bit_adder_3 (
    .A(A[7:4]), .B(B[7:4]), .Cin(four_bit_adder_1_cout), .S(C[7:4]), .Cout(four_bit_adder_3_cout));
  Four_Bit_Adder four_bit_adder_4 (
    .A(A[23:20]), .B(B[23:20]), .Cin(four_bit_adder_2_cout), .S(C[23:20]), .Cout(four_bit_adder_4_cout));
  Four_Bit_Adder four_bit_adder_5 (
    .A(A[11:8]), .B(B[11:8]), .Cin(four_bit_adder_3_cout), .S(C[11:8]), .Cout(four_bit_adder_5_cout));
  Four_Bit_Adder four_bit_adder_6 (
    .A(A[27:24]), .B(B[27:24]), .Cin(four_bit_adder_4_cout), .S(C[27:24]), .Cout(four_bit_adder_6_cout));
  Four_Bit_Adder four_bit_adder_7 (
    .A(A[15:12]), .B(B[15:12]), .Cin(four_bit_adder_5_cout), .S(C[15:12]), .Cout(four_bit_adder_7_cout));
  Signed_Four_Bit_Adder signed_four_bit_adder_1 (
    .A(A[31:28]), .B(B[31:28]), .Cin(four_bit_adder_6_cout), .S(C[31:28]), .V(V));  // open: Cout
endmodule

module main (
  input  A,
  input  B,
  input  Cin,
  output S,
  output Cout
);

  wire and_1_out, and_2_out, xor_1_out;

  xor xor_1 (xor_1_out, A, B);
  and and_1 (and_1_out, xor_1_out, Cin);
  and and_2 (and_2_out, A, B);
  xor xor_2 (S, xor_1_out, Cin);
  or or_1 (Cout, and_1_out, and_2_out);

  // Notes on the sheet:
  //   One Bit Adder
endmodule

module Four_Bit_Adder (
  input  [3:0] A,
  input  [3:0] B,
  input  Cin,
  output [3:0] S,
  output Cout
);

  wire main_1_cout, main_2_cout, main_3_cout;

  main main_1 (.A(A[0]), .B(B[0]), .Cin(Cin), .S(S[0]), .Cout(main_1_cout));
  main main_2 (.A(A[1]), .B(B[1]), .Cin(main_1_cout), .S(S[1]), .Cout(main_2_cout));
  main main_3 (.A(A[2]), .B(B[2]), .Cin(main_2_cout), .S(S[2]), .Cout(main_3_cout));
  main main_4 (.A(A[3]), .B(B[3]), .Cin(main_3_cout), .S(S[3]), .Cout(Cout));
endmodule

module Signed_Four_Bit_Adder (
  input  [3:0] A,
  input  [3:0] B,
  input  Cin,
  output [3:0] S,
  output V,
  output Cout
);

  wire main_1_cout, main_2_cout, main_3_cout;

  main main_1 (.A(A[0]), .B(B[0]), .Cin(Cin), .S(S[0]), .Cout(main_1_cout));
  main main_2 (.A(A[1]), .B(B[1]), .Cin(main_1_cout), .S(S[1]), .Cout(main_2_cout));
  main main_3 (.A(A[2]), .B(B[2]), .Cin(main_2_cout), .S(S[2]), .Cout(main_3_cout));
  main main_4 (.A(A[3]), .B(B[3]), .Cin(main_3_cout), .S(S[3]), .Cout(Cout));
  xor xor_1 (V, main_3_cout, Cout);
endmodule

module ALU32 (
  input  [31:0] A,
  input  [31:0] B,
  input  [4:0] Sa,
  input  [3:0] Op,
  output [31:0] C,
  output V
);

  wire and_2_out, multiplexer_5_out, multiplexer_7_out, multiplexer_8_out, not_2_out, not_3_out, not_4_out,
       or32_1_cout, or32_2_cout, signedbit32_1_cout, signedbit32_2_cout, xnor_1_out;
  wire [0:0] multiplexer_10_out;
  wire [31:0] add32_1_c, and_1_out, flip32_1_cout, flip32_2_cout, leftshift32_1_c, multiplexer_1_out,
       multiplexer_2_out, multiplexer_3_out, multiplexer_4_out, multiplexer_6_out, multiplexer_9_out,
       multiplexer_11_out, multiplexer_12_out, nor_1_out, not_1_out, or_1_out, xor_1_out;

  assign not_1_out = ~B;  // NOT_Gate not_1, 32 bits wide
  Flip32 flip32_1 (.Cin(B), .Cout(flip32_1_cout));
  Multiplexer #(.width(32), .enable("false")) multiplexer_1 (
    .in0(not_1_out), .in1(B), .out(multiplexer_1_out), .sel(Op[1]));
  assign and_1_out = A & B;  // AND_Gate and_1, 32 bits wide
  assign or_1_out = A | B;  // OR_Gate or_1, 32 bits wide
  assign xor_1_out = A ^ B;  // XOR_Gate xor_1, 32 bits wide
  assign nor_1_out = ~(A | B);  // NOR_Gate nor_1, 32 bits wide
  Multiplexer #(.width(32), .enable("false")) multiplexer_2 (
    .in0(B), .in1(flip32_1_cout), .out(multiplexer_2_out), .sel(Op[2]));
  SignedBit32 signedbit32_1 (.Cin(flip32_1_cout), .Cout(signedbit32_1_cout));
  Or32 or32_1 (.Cin(A), .Cout(or32_1_cout));
  not not_2 (not_2_out, Op[1]);
  Multiplexer #(.width(32), .enable("false")) multiplexer_3 (
    .in0(and_1_out), .in1(or_1_out), .out(multiplexer_3_out), .sel(Op[0]));
  Multiplexer #(.width(32), .enable("false")) multiplexer_4 (
    .in0(xor_1_out), .in1(nor_1_out), .out(multiplexer_4_out), .sel(Op[0]));
  SignedBit32 signedbit32_2 (.Cin(A), .Cout(signedbit32_2_cout));
  Multiplexer #(.enable("false")) multiplexer_5 (
    .in1(signedbit32_1_cout), .out(multiplexer_5_out), .sel(and_2_out));  // open: in0
  and and_2 (and_2_out, Op[0], Op[1]);
  xnor xnor_1 (xnor_1_out, signedbit32_2_cout, or32_1_cout);
  Add32 add32_1 (.A(A), .Cin(not_2_out), .B(multiplexer_1_out), .C(add32_1_c), .V(V));
  Multiplexer #(.width(32), .enable("false")) multiplexer_6 (
    .in0(multiplexer_3_out), .in1(multiplexer_4_out), .out(multiplexer_6_out), .sel(Op[3]));
  Or32 or32_2 (.Cin(xor_1_out), .Cout(or32_2_cout));
  not not_3 (not_3_out, or32_2_cout);
  LeftShift32 leftshift32_1 (.B(multiplexer_2_out), .Sa(Sa), .Cin(multiplexer_5_out), .C(leftshift32_1_c));
  not not_4 (not_4_out, xnor_1_out);
  Multiplexer #(.enable("false")) multiplexer_7 (
    .in0(or32_2_cout), .in1(not_3_out), .out(multiplexer_7_out), .sel(Op[0]));
  Multiplexer #(.enable("false")) multiplexer_8 (
    .in0(xnor_1_out), .in1(not_4_out), .out(multiplexer_8_out), .sel(Op[0]));
  Flip32 flip32_2 (.Cin(leftshift32_1_c), .Cout(flip32_2_cout));
  Multiplexer #(.width(32), .enable("false")) multiplexer_9 (
    .in0(multiplexer_6_out), .in1(multiplexer_11_out), .out(multiplexer_9_out), .sel(Op[1]));
  Multiplexer #(.enable("false")) multiplexer_10 (
    .in0(multiplexer_7_out), .in1(multiplexer_8_out), .out(multiplexer_10_out[0]), .sel(Op[1]));
  Multiplexer #(.width(32), .enable("false")) multiplexer_11 (
    .in0(leftshift32_1_c), .in1(flip32_2_cout), .out(multiplexer_11_out), .sel(Op[2]));
  Multiplexer #(.width(32), .enable("false")) multiplexer_12 (
    .in0({{31{1'b0}}, multiplexer_10_out[0]}), .in1(add32_1_c), .out(multiplexer_12_out), .sel(Op[2]));
  Multiplexer #(.width(32), .enable("false")) multiplexer_13 (
    .in0(multiplexer_9_out), .in1(multiplexer_12_out), .out(C), .sel(Op[3]));
endmodule

module Flip32 (
  input  [31:0] Cin,
  output [31:0] Cout
);


  assign Cout = {Cin[0], Cin[1], Cin[2], Cin[3], Cin[4], Cin[5], Cin[6], Cin[7], Cin[8], Cin[9], Cin[10], Cin[11], Cin[12], Cin[13], Cin[14], Cin[15], Cin[16], Cin[17], Cin[18], Cin[19], Cin[20], Cin[21], Cin[22], Cin[23], Cin[24], Cin[25], Cin[26], Cin[27], Cin[28], Cin[29], Cin[30], Cin[31]};
endmodule

module SignedBit32 (
  input  [31:0] Cin,
  output Cout
);


  assign Cout = Cin[31];
endmodule

module Or32 (
  input  [31:0] Cin,
  output Cout
);

  or or_1 (Cout, Cin[0], Cin[1], Cin[2], Cin[3], Cin[4], Cin[5], Cin[6], Cin[7], Cin[8], Cin[9], Cin[10], Cin[11], Cin[12], Cin[13], Cin[14], Cin[15], Cin[16], Cin[17], Cin[18], Cin[19], Cin[20], Cin[21], Cin[22], Cin[23], Cin[24], Cin[25], Cin[26], Cin[27], Cin[28], Cin[29], Cin[30], Cin[31]);
endmodule
